# Fritzing sketch Sensor (saved by Fritzing 0.9.3b)
circuit board: 8.46667cm x 5.64444cm
breadboards: 1

parts:
  Componente1 = Arduino Uno (Rev3)
  J1 = Piezo Speaker
  LED1 = LED - 5mm [color="Red (633nm)" package="5 mm [THT]"]
  LED2 = LED - 5mm [color="Red (633nm)" package="5 mm [THT]"]
  LED3 = LED - 5mm [color="Red (633nm)" package="5 mm [THT]"]
  R1 = Resistor [tolerance=±5% resistance=330 package=THT]
  R2 = Resistor [tolerance=±5% resistance=330 package=THT]
  R3 = Resistor [tolerance=±5% resistance=330 package=THT]
  Componente2 = HC-SR501 Body Sensor Module

nets:
  N1: Componente1.D8, J1.pin2
  N2: Componente1.D13/SCK, Componente2.OUT
  GND: Componente1.GND, J1.pin1, LED1.cathode, LED2.cathode, LED3.cathode, Componente2.GND
  N3: Componente1.D2, R3.Pin_1
  N4: Componente1.D4, R2.Pin_1
  N5: Componente1.D6_PWM, R1.Pin_1
  5V: Componente1.5V, Componente2.VCC
  N6: LED1.anode, R1.Pin_0
  N7: LED2.anode, R2.Pin_0
  N8: LED3.anode, R3.Pin_0

custom parts:
  HC-SR501 Body Sensor Module: Pyroelectric Infrared PIR Motion Sensor Detector Module

// code stored in the sketch: Sensor_movimiento.ino
#define PIRSENSOR 13
#define BUZZER 8
#define LED1 6 
#define LED2 4 
#define LED3 2 

void setup()
{
  pinMode(BUZZER, OUTPUT);
  pinMode(LED1, OUTPUT); 
  pinMode(LED2, OUTPUT);
  pinMode(LED3, OUTPUT);
  pinMode(PIRSENSOR, INPUT);
  }
void loop() 
{ 
  if(digitalRead(PIRSENSOR) == HIGH)
{
  digitalWrite(BUZZER, HIGH); 
  digitalWrite(LED1, HIGH);
  digitalWrite(LED2, HIGH);
  digitalWrite(LED3, HIGH);
  delay(3000);
} 
else
{ 
  digitalWrite(BUZZER, LOW);
  digitalWrite(LED1, LOW);
  digitalWrite(LED2, LOW); 
  digitalWrite(LED3, LOW); 
  }

}
